# Fritzing sketch rgb-led (saved by Fritzing 0.9.3b)
breadboards: 1

parts:
  LED1 = smd LED [color="Red (633nm)" package="1206 [SMD]"]  # not connected
  LED2 = smd LED [color="Red (633nm)" package="1206 [SMD]"]
  LED3 = smd LED [color="Red (633nm)" package="1206 [SMD]"]
  LED9 = smd LED [color="Red (633nm)" package="1206 [SMD]"]  # not connected
  LED10 = smd LED [color="Red (633nm)" package="1206 [SMD]"]
  LED12 = smd LED [color="Red (633nm)" package="1206 [SMD]"]

nets:
  N1: LED2.anode, LED3.anode
  N2: LED10.cathode, LED12.cathode

notes:
  Common Anode
  ROW 5
  ROW 3
  ROW 8
  ROW 6
  ROW 4
  ROW 1
  ROW 7
  R
  G
  B
  A
  D
  C
  F
  E
  H
  Common Cathode
