# Fritzing sketch 74NC595-led-number (saved by Fritzing 0.9.3b)
circuit board: 8.46667cm x 5.64444cm
breadboards: 1

parts:
  DI1 = 7-Segment LED Display [package=THT]
  U1 = 74HC595 SMD [package="SO16 [SMD]"]
  Raspberry_Pi_1 = Raspberry Pi 3 [part_number=RPI-3-V1.2]
  R1 = Resistor [tolerance=±5% resistance=330 package="2010 [SMD]"]
  R2 = Resistor [tolerance=±5% resistance=330 package="2010 [SMD]"]
  R3 = Resistor [tolerance=±5% resistance=330 package="2010 [SMD]"]
  R4 = Resistor [tolerance=±5% resistance=330 package="2010 [SMD]"]
  R5 = Resistor [tolerance=±5% resistance=330 package="2010 [SMD]"]
  R6 = Resistor [tolerance=±5% resistance=330 package="2010 [SMD]"]
  R7 = Resistor [tolerance=±5% resistance=330 package="2010 [SMD]"]
  R8 = Resistor [tolerance=±5% resistance=330 package="2010 [SMD]"]

nets:
  N1: DI1.cathodeE, R5.Pin_1
  N2: DI1.cathodeD, R6.Pin_1
  N3: DI1.cathodeC, R4.Pin_0
  N4: DI1.cathodeDP, R3.Pin_0
  N5: DI1.cathodeB, R2.Pin_0
  N6: DI1.cathodeA, R1.Pin_0
  GND: DI1.commAnode#7, U1.GND, U1.OE, Raspberry_Pi_1.GND
  N7: DI1.cathodeF, R8.Pin_1
  N8: DI1.cathodeG, R7.Pin_1
  N9: U1.Q1, R2.Pin_1
  N10: U1.Q2, R4.Pin_1
  N11: U1.Q3, R6.Pin_0
  N12: U1.Q4, R5.Pin_0
  N13: U1.Q5, R8.Pin_0
  N14: U1.Q6, R7.Pin_0
  N15: U1.Q7, R3.Pin_1
  3V3: U1.MR, U1.VCC, Raspberry_Pi_1.3v3, Raspberry_Pi_1.3V3
  N16: U1.SH_CP, Raspberry_Pi_1.GPIO5
  N17: U1.ST_CP, Raspberry_Pi_1.GPIO6
  N18: U1.DS, Raspberry_Pi_1.GPIO4
  N19: U1.Q0, R1.Pin_1
