# Fritzing sketch segment-display (saved by Fritzing 0.9.3b)
breadboards: 1

parts:
  LED1 = smd LED [color="Red (633nm)" package="1206 [SMD]"]  # not connected
  LED2 = smd LED [color="Red (633nm)" package="1206 [SMD]"]
  LED3 = smd LED [color="Red (633nm)" package="1206 [SMD]"]  # not connected
  LED4 = smd LED [color="Red (633nm)" package="1206 [SMD]"]  # not connected
  LED5 = smd LED [color="Red (633nm)" package="1206 [SMD]"]  # not connected
  LED6 = smd LED [color="Red (633nm)" package="1206 [SMD]"]  # not connected
  LED7 = smd LED [color="Red (633nm)" package="1206 [SMD]"]
  LED8 = smd LED [color="Red (633nm)" package="1206 [SMD]"]  # not connected
  LED9 = smd LED [color="Red (633nm)" package="1206 [SMD]"]  # not connected
  LED10 = smd LED [color="Red (633nm)" package="1206 [SMD]"]
  LED11 = smd LED [color="Red (633nm)" package="1206 [SMD]"]  # not connected
  LED12 = smd LED [color="Red (633nm)" package="1206 [SMD]"]  # not connected
  LED13 = smd LED [color="Red (633nm)" package="1206 [SMD]"]  # not connected
  LED14 = smd LED [color="Red (633nm)" package="1206 [SMD]"]  # not connected
  LED15 = smd LED [color="Red (633nm)" package="1206 [SMD]"]
  LED16 = smd LED [color="Red (633nm)" package="1206 [SMD]"]  # not connected

nets:
  N1: LED2.anode, LED7.anode
  N2: LED10.cathode, LED15.cathode

notes:
  Common Anode
  ROW 5
  ROW 3
  ROW 8
  ROW 6
  ROW 4
  ROW 1
  ROW 7
  A
  B
  C
  D
  E
  F
  G
  H
  Common Cathode
