# Fritzing sketch 8x8-led-matrix (saved by Fritzing 0.9.3b)
breadboards: 1

parts:
  LED1 = smd LED [color="Red (633nm)" package="1206 [SMD]"]
  LED2 = smd LED [color="Red (633nm)" package="1206 [SMD]"]
  LED3 = smd LED [color="Red (633nm)" package="1206 [SMD]"]
  LED4 = smd LED [color="Red (633nm)" package="1206 [SMD]"]
  LED5 = smd LED [color="Red (633nm)" package="1206 [SMD]"]
  LED6 = smd LED [color="Red (633nm)" package="1206 [SMD]"]
  LED7 = smd LED [color="Red (633nm)" package="1206 [SMD]"]
  LED8 = smd LED [color="Red (633nm)" package="1206 [SMD]"]
  LED9 = smd LED [color="Red (633nm)" package="1206 [SMD]"]
  LED10 = smd LED [color="Red (633nm)" package="1206 [SMD]"]
  LED11 = smd LED [color="Red (633nm)" package="1206 [SMD]"]
  LED12 = smd LED [color="Red (633nm)" package="1206 [SMD]"]
  LED13 = smd LED [color="Red (633nm)" package="1206 [SMD]"]
  LED14 = smd LED [color="Red (633nm)" package="1206 [SMD]"]
  LED15 = smd LED [color="Red (633nm)" package="1206 [SMD]"]
  LED16 = smd LED [color="Red (633nm)" package="1206 [SMD]"]
  LED17 = smd LED [color="Red (633nm)" package="1206 [SMD]"]
  LED18 = smd LED [color="Red (633nm)" package="1206 [SMD]"]
  LED19 = smd LED [color="Red (633nm)" package="1206 [SMD]"]
  LED20 = smd LED [color="Red (633nm)" package="1206 [SMD]"]
  LED21 = smd LED [color="Red (633nm)" package="1206 [SMD]"]
  LED22 = smd LED [color="Red (633nm)" package="1206 [SMD]"]
  LED23 = smd LED [color="Red (633nm)" package="1206 [SMD]"]
  LED24 = smd LED [color="Red (633nm)" package="1206 [SMD]"]
  LED25 = smd LED [color="Red (633nm)" package="1206 [SMD]"]
  LED26 = smd LED [color="Red (633nm)" package="1206 [SMD]"]
  LED27 = smd LED [color="Red (633nm)" package="1206 [SMD]"]
  LED28 = smd LED [color="Red (633nm)" package="1206 [SMD]"]
  LED29 = smd LED [color="Red (633nm)" package="1206 [SMD]"]
  LED30 = smd LED [color="Red (633nm)" package="1206 [SMD]"]
  LED31 = smd LED [color="Red (633nm)" package="1206 [SMD]"]
  LED32 = smd LED [color="Red (633nm)" package="1206 [SMD]"]
  LED33 = smd LED [color="Red (633nm)" package="1206 [SMD]"]
  LED34 = smd LED [color="Red (633nm)" package="1206 [SMD]"]
  LED35 = smd LED [color="Red (633nm)" package="1206 [SMD]"]
  LED36 = smd LED [color="Red (633nm)" package="1206 [SMD]"]
  LED37 = smd LED [color="Red (633nm)" package="1206 [SMD]"]
  LED38 = smd LED [color="Red (633nm)" package="1206 [SMD]"]
  LED39 = smd LED [color="Red (633nm)" package="1206 [SMD]"]
  LED40 = smd LED [color="Red (633nm)" package="1206 [SMD]"]
  LED41 = smd LED [color="Red (633nm)" package="1206 [SMD]"]
  LED42 = smd LED [color="Red (633nm)" package="1206 [SMD]"]
  LED43 = smd LED [color="Red (633nm)" package="1206 [SMD]"]
  LED44 = smd LED [color="Red (633nm)" package="1206 [SMD]"]
  LED45 = smd LED [color="Red (633nm)" package="1206 [SMD]"]
  LED46 = smd LED [color="Red (633nm)" package="1206 [SMD]"]
  LED47 = smd LED [color="Red (633nm)" package="1206 [SMD]"]
  LED48 = smd LED [color="Red (633nm)" package="1206 [SMD]"]
  LED49 = smd LED [color="Red (633nm)" package="1206 [SMD]"]
  LED50 = smd LED [color="Red (633nm)" package="1206 [SMD]"]
  LED51 = smd LED [color="Red (633nm)" package="1206 [SMD]"]
  LED52 = smd LED [color="Red (633nm)" package="1206 [SMD]"]
  LED53 = smd LED [color="Red (633nm)" package="1206 [SMD]"]
  LED54 = smd LED [color="Red (633nm)" package="1206 [SMD]"]
  LED55 = smd LED [color="Red (633nm)" package="1206 [SMD]"]
  LED56 = smd LED [color="Red (633nm)" package="1206 [SMD]"]
  LED57 = smd LED [color="Red (633nm)" package="1206 [SMD]"]
  LED58 = smd LED [color="Red (633nm)" package="1206 [SMD]"]
  LED59 = smd LED [color="Red (633nm)" package="1206 [SMD]"]
  LED60 = smd LED [color="Red (633nm)" package="1206 [SMD]"]
  LED61 = smd LED [color="Red (633nm)" package="1206 [SMD]"]
  LED62 = smd LED [color="Red (633nm)" package="1206 [SMD]"]
  LED63 = smd LED [color="Red (633nm)" package="1206 [SMD]"]
  LED64 = smd LED [color="Red (633nm)" package="1206 [SMD]"]

nets:
  N1: LED1.cathode, LED12.cathode
  N2: LED2.cathode, LED10.cathode
  N3: LED2.anode, LED7.anode
  N4: LED3.cathode, LED14.cathode
  N5: LED4.cathode, LED15.cathode
  N6: LED5.cathode, LED13.cathode
  N7: LED6.cathode, LED9.cathode
  N8: LED7.cathode, LED11.cathode
  N9: LED8.cathode, LED16.cathode
  N10: LED10.anode, LED11.anode
  N11: LED17.cathode, LED22.cathode
  N12: LED18.cathode, LED32.cathode
  N13: LED19.cathode, LED21.cathode
  N14: LED20.cathode, LED25.cathode
  N15: LED20.anode, LED27.anode
  N16: LED23.cathode, LED30.cathode
  N17: LED24.cathode, LED31.cathode
  N18: LED25.anode, LED28.anode
  N19: LED26.cathode, LED29.cathode
  N20: LED27.cathode, LED28.cathode
  N21: LED33.cathode, LED56.cathode
  N22: LED34.cathode, LED42.cathode
  N23: LED35.cathode, LED55.cathode
  N24: LED36.cathode, LED47.cathode
  N25: LED36.anode, LED48.anode
  N26: LED37.cathode, LED45.cathode
  N27: LED38.cathode, LED39.cathode
  N28: LED38.anode, LED63.anode
  N29: LED39.anode, LED59.anode
  N30: LED40.cathode, LED51.cathode
  N31: LED41.cathode, LED58.cathode
  N32: LED43.cathode, LED48.cathode
  N33: LED43.anode, LED47.anode
  N34: LED44.cathode, LED52.cathode
  N35: LED46.cathode, LED50.cathode
  N36: LED49.cathode, LED64.cathode
  N37: LED53.cathode, LED54.cathode
  N38: LED57.cathode, LED62.cathode
  N39: LED59.cathode, LED63.cathode
  N40: LED60.cathode, LED61.cathode

notes:
  ROW 1
  ROW 2
  ROW 3
  ROW 4
  ROW 5
  ROW 6
  ROW 7
  ROW 8
  COL 1
  COL 2
  COL 3
  COL 4
  COL 5
  COL 6
  COL 7
  COL 8
