# Fritzing sketch digital-output-led-multiple-resistors (saved by Fritzing 0.9.3b)
breadboards: 1

parts:
  Raspberry_Pi_1 = Raspberry Pi 3 [part_number=RPI-3-V1.2]
  LED3 = RGB LED (com. cathode, rgb) [package="5 mm [THT]"]
  R1 = Resistor [tolerance=±5% resistance=220 package=THT]
  R2 = Resistor [tolerance=±5% resistance=100 package=THT]
  R3 = Resistor [tolerance=±5% resistance=100 package=THT]

nets:
  N1: Raspberry_Pi_1.GND, LED3.common_cathode
  N2: Raspberry_Pi_1.GPIO11, R3.Pin_0
  N3: Raspberry_Pi_1.GPIO13, R1.Pin_0
  N4: Raspberry_Pi_1.GPIO14, R2.Pin_0
  N5: LED3.red_anode, R1.Pin_1
  N6: LED3.green_anode, R2.Pin_1
  N7: LED3.blue_anode, R3.Pin_1
