# Fritzing sketch digital-output-led-one-resistor_v3 (saved by Fritzing 1.0.4)
breadboards: 1

parts:
  R1 = Resistor [tolerance=±5% resistance=330 package="0603 [SMD]"]
  LED3 = RGB LED (com. cathode, rgb) [color="Red (633nm)" current=0.030A package="5 mm [THT]"]
  Mod1 = Raspberry Pi 4B

nets:
  N1: R1.Pin_0, Mod1.GND
  N2: R1.Pin_1, LED3.common_cathode
  N3: LED3.red_anode, Mod1.GPIO13
  N4: LED3.green_anode, Mod1.GPIO12
  N5: LED3.blue_anode, Mod1.GPIO11
