# Fritzing sketch digital-output-led (saved by Fritzing 0.9.3b)
breadboards: 1

parts:
  Raspberry_Pi_1 = Raspberry Pi 3 [part_number=RPI-3-V1.2]
  LED3 = RGB LED (com. cathode, rgb) [package="5 mm [THT]"]
  R1 = Resistor [tolerance=±5% resistance=330 package="0603 [SMD]"]

nets:
  N1: Raspberry_Pi_1.GPIO11, LED3.blue_anode
  N2: Raspberry_Pi_1.GPIO13, LED3.red_anode
  N3: Raspberry_Pi_1.GPIO14, LED3.green_anode
  N4: Raspberry_Pi_1.GND, R1.Pin_0
  N5: LED3.common_cathode, R1.Pin_1
