# Fritzing sketch lcd (saved by Fritzing 0.9.3b)
breadboards: 1

parts:
  Raspberry_Pi_1 = Raspberry Pi 3 [part_number=RPI-3-V1.2]
  LCD1 = LCD screen
  R1 = Rotary Potentiometer (Small) [maximum_resistance=100kΩ package=THT]
  R2 = Rotary Potentiometer (Small) [maximum_resistance=100kΩ package=THT]

nets:
  N1: Raspberry_Pi_1.GIPO17, LCD1.DB5
  N2: Raspberry_Pi_1.GIPO22, LCD1.DB7
  GND: Raspberry_Pi_1.GND, LCD1.VSS, LCD1.R/W, LCD1.LED-, R2.wiper
  N3: Raspberry_Pi_1.GIPO25, LCD1.RS
  N4: Raspberry_Pi_1.GIPO24, LCD1.E
  N5: Raspberry_Pi_1.GIPO23, LCD1.DB4
  N6: Raspberry_Pi_1.GIPO18, LCD1.DB6
  5V: Raspberry_Pi_1.5V, LCD1.VDD, R1.wiper
  N7: LCD1.V0, R2.leg1
  N8: LCD1.LED+, R1.leg2
