# Fritzing sketch serial-arduino-lightsensor (saved by Fritzing 0.9.3b)
breadboards: 1

parts:
  Raspberry_Pi_1 = Raspberry Pi 3 [part_number=RPI-3-V1.2]  # not connected
  R1 = Photocell (LDR) [package=THT]
  R2 = Resistor [tolerance=±5% resistance=10k package="0603 [SMD]"]
  Onderdeel1 = Arduino Uno (Rev3)

nets:
  N1: R1.pin_0, R2.Pin_1, Onderdeel1.A0
  N2: R1.pin_1, Onderdeel1.5V
  N3: R2.Pin_0, Onderdeel1.GND
