# Fritzing sketch spi-max7219 (saved by Fritzing 0.9.3b)

parts:
  Raspberry_Pi_1 = Raspberry Pi 3 [part_number=RPI-3-V1.2]
  Part1 = LED Matrix - Serial Interface - Red/Green/Blue

nets:
  N1: Raspberry_Pi_1.GIPO10, Part1.MISO
  N2: Raspberry_Pi_1.GIPO11, Part1.SCK
  GND: Raspberry_Pi_1.GND, Part1.GND
  N3: Raspberry_Pi_1.GIPO8, Part1.CS
  5V: Raspberry_Pi_1.5V, Part1.VCC
