# Fritzing sketch arduino-ledstrip (saved by Fritzing 0.9.3b)

parts:
  RGB_Led_strip = ws2812b [package="smd 2812b"]
  Arduino_Uni_WiFi_REV2 = Arduino Uno (Rev3)
  Power_supply = DC Power [voltage=5V]

nets:
  VDD: RGB_Led_strip.VDD, Arduino_Uni_WiFi_REV2.5V, Power_supply.V+
  VSS: RGB_Led_strip.VSS, Arduino_Uni_WiFi_REV2.GND, Power_supply.V-
  N1: RGB_Led_strip.DIN, Arduino_Uni_WiFi_REV2.D6_PWM
